# Fritzing sketch Arduino Uno with RFID RC522 (saved by Fritzing 0.9.3b)

parts:
  Part3 = Arduino Uno (Rev3)
  Part2 = RFID-RC522-v2

nets:
  N1: Part3.D9_PWM, Part2.RST
  N2: Part3.D10_PWM/SS, Part2.SDA
  N3: Part3.D11_PWM/MOSI, Part2.MOSI
  N4: Part3.D12/MISO, Part2.MISO
  N5: Part3.D13/SCK, Part2.SCK
  N6: Part3.3V3, Part2.3_3V
  GND: Part3.GND, Part2.GND

custom parts:
  RFID-RC522-v2: A simple China made RFID-RC522 Reader; do check the pin labels, as this is a MFRC522 based clone.
